# Fritzing sketch led (saved by Fritzing 0.9.3b)
circuit board: 6.85724cm x 5.34267cm
breadboards: 1

parts:
  R1 = Resistor [tolerance=±5% resistance=330 package=THT]
  LED1 = LED - 5mm [color="Red (633nm)" package="5 mm [THT]"]
  Componente1 = Arduino Uno (Rev3)

nets:
  N1: R1.Pin_0, LED1.anode
  N2: R1.Pin_1, Componente1.D13/SCK
  N3: LED1.cathode, Componente1.GND
